# Fritzing sketch serial_LCD_reactionTimer (saved by Fritzing 0.9.3b)
breadboards: 1

parts:
  Parts1 = SparkFun RedBoard [part_number=DEV-12757]
  S1 = Colored SIK Pushbutton [part_number=COM-10302 package=PTH]
  LED1 = LED - 5mm [color="Red (633nm)" package="5 mm [THT]"]
  R1 = Resistor [tolerance=±5% resistance=330 package="1206 [SMD]"]
  LCD1 = LCD screen
  R2 = TSR-3386UT Square Trimming Potentiometer [part_number=TSR-3386]

nets:
  N1: Parts1.D8, LCD1.RS
  N2: Parts1.D9_PWM, LCD1.E
  N3: Parts1.D10_PWM/SS, LCD1.DB4
  N4: Parts1.D11_PWM/MOSI, LCD1.DB5
  N5: Parts1.D12/MISO, LCD1.DB6
  N6: Parts1.D13/SCK, LCD1.DB7
  GND: Parts1.GND, S1.Pin_1, S1.Pin_3, R1.Pin_0, LCD1.VSS, LCD1.R/W, LCD1.LED-, R2.Leg2
  N7: Parts1.D2, S1.Pin_2, S1.Pin_4
  N8: Parts1.D5_PWM, LED1.anode
  5V: Parts1.5V, LCD1.VDD, LCD1.LED+, R2.Leg1
  N9: LED1.cathode, R1.Pin_1
  N10: LCD1.V0, R2.wiper

custom parts:
  SparkFun RedBoard: At SparkFun we use many Arduinos and we’re always looking for the simplest, most stable one. Each board is a bit different and no one board has everything we want, so we decided to make our own version that combines all our favorite features. The RedBoard combines the simplicity of the UNO’s Optiboot bootloader (which is used in the Pro series), the stability of the FTDI (which we all missed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
  Colored SIK Pushbutton: A generic pushbutton.
  LCD screen: A standard character display, usually with 2x16 characters. Comes in many colors.
  TSR-3386UT Square Trimming Potentiometer: Trimpot 10K with Knob
